# Fritzing sketch 7-Segment counter (saved by Fritzing 0.7.0b)
breadboards: 1

parts:
  Netduino1 = Netduino
  DI1 = 7-Segment LED Display [package=THT]
  R1 = Resistor [tolerance=±5% resistance=220 package=THT]
  R2 = Resistor [tolerance=±5% resistance=220 package=THT]
  R3 = Resistor [tolerance=±5% resistance=220 package=THT]
  R4 = Resistor [tolerance=±5% resistance=220 package=THT]
  R5 = Resistor [tolerance=±5% resistance=220 package=THT]
  R6 = Resistor [tolerance=±5% resistance=220 package=THT]
  R7 = Resistor [tolerance=±5% resistance=220 package=THT]
  R8 = Resistor [tolerance=±5% resistance=220 package=THT]
  IC1 = IC, DIP package, 16 pins [chip_label=74HC595 spacing=300mil]

nets:
  N1: Netduino1.GND, IC1.pin8, IC1.pin13
  N2: Netduino1.D13_SPCK, IC1.pin11
  N3: Netduino1.D11_MOSI, IC1.pin14
  N4: Netduino1.D10_PWM3, IC1.pin12
  N5: Netduino1.3V3, DI1.commAnode, IC1.pin10, IC1.pin16
  N6: DI1.cathodeE, R1.Pin_1
  N7: DI1.cathodeD, R2.Pin_1
  N8: DI1.cathodeC, R3.Pin_1
  N9: DI1.cathodeDP, R4.Pin_1
  N10: DI1.cathodeB, R5.Pin_1
  N11: DI1.cathodeA, R6.Pin_1
  N12: DI1.cathodeF, R7.Pin_1
  N13: DI1.cathodeG, R8.Pin_1
  N14: R1.Pin_0, IC1.pin15
  N15: R2.Pin_0, IC1.pin1
  N16: R3.Pin_0, IC1.pin2
  N17: R4.Pin_0, IC1.pin3
  N18: R5.Pin_0, IC1.pin4
  N19: R6.Pin_0, IC1.pin5
  N20: R7.Pin_0, IC1.pin6
  N21: R8.Pin_0, IC1.pin7
