# Fritzing sketch Bar Graph Breakout Kit (saved by Fritzing 0.7.0b)
perfboards: 1

parts:
  Netduino1 = Netduino
  J1 = female pin header, 6 pins [form="♂ (male)"]

nets:
  N1: Netduino1.D12_MISO, J1.pin2
  N2: Netduino1.D11_MOSI, J1.pin4
  N3: Netduino1.D10_PWM3, J1.pin3
  N4: Netduino1.+5V, J1.pin6
  N5: Netduino1.GND, J1.pin5
