# Fritzing sketch DS1307 RTC Module (saved by Fritzing 0.7.4b)
breadboards: 1

parts:
  Netduino2 = Netduino
  IC1 = IC, DIP package, 8 pins [chip_label=DS1307 spacing=300mil]
  R1 = Resistor [tolerance=±5% resistance=10k package=THT]
  R2 = Resistor [tolerance=±5% resistance=10k package=THT]
  XTAL1 = CRYSTAL - kHz [frequency="32 kHz"]
  VCC1 = Battery

nets:
  N1: Netduino2.+5V, IC1.pin8, R1.Pin_1, R2.Pin_1
  N2: Netduino2.GND, IC1.pin4, VCC1.-
  N3: Netduino2.A4_TWD, IC1.pin5, R1.Pin_0
  N4: Netduino2.A5_TWCK, IC1.pin6, R2.Pin_0
  N5: IC1.pin1, XTAL1.pin_1
  N6: IC1.pin2, XTAL1.pin_0
  N7: IC1.pin3, VCC1.+
