# Fritzing sketch HD44780 LCD (saved by Fritzing 0.7.4b)
breadboards: 1

parts:
  LCD1 = LCD screen
  Netduino1 = Netduino
  R1 = Rotary Potentiometer (Small) [maximum_resistance=100kΩ]

nets:
  VSS: LCD1.VSS, LCD1.R/W, LCD1.LED-, Netduino1.GND, R1.leg1
  VDD: LCD1.VDD, LCD1.LED+, Netduino1.3V3, R1.leg2
  N1: LCD1.V0, R1.wiper
  N2: LCD1.RS, Netduino1.D8_CTS1
  N3: LCD1.E, Netduino1.D9_PWM2
  N4: LCD1.DB4, Netduino1.D4_CS0
  N5: LCD1.DB5, Netduino1.D5_PWM0
  N6: LCD1.DB6, Netduino1.D6_PWM1
  N7: LCD1.DB7, Netduino1.D7_RTS1

notes:
  Most LCDs use this pin layout:
  1 Gnd
  2 Vcc
  3 Contrast
  4 Register Select
  5 Read/Write Select
  6 Chip Enable
  7 Databit 0
  8 Databit 1
  9 Databit 2
  10 Databit 3
  11 Databit 4
  12 Databit 5
  13 Databit 6
  14 Databit 7
  15 Background LED +
  16 Background LED -
