# Fritzing sketch LED RingCoder Breakout (saved by Fritzing 0.7.0b)
perfboards: 1
breadboards: 1

parts:
  J1 = female pin header, 12 pins [form="♂ (male)"]  # not connected
  Netduino1 = Netduino
  R1 = Resistor [tolerance=±5% resistance=220 package="0603 [SMD]"]
  R2 = Resistor [tolerance=±5% resistance=220 package="0603 [SMD]"]

nets:
  N1: Netduino1.D4_CS0, R1.Pin_1
  N2: Netduino1.D3_TX1, R2.Pin_1
