# Fritzing sketch LPD8806 RGB Strip with Chip Select (saved by Fritzing 0.7.4b)
breadboards: 1

parts:
  VCC1 = 4 x AAA Battery Mount
  J1 = male pin header, 4 pins [form="♂ (male)"]
  Netduino1 = Netduino
  MOSFET = NPN-Transistor [package="TO92 [THT]"]

nets:
  N1: VCC1.-, J1.pin1, Netduino1.GND
  N2: VCC1.+, J1.pin4
  N3: J1.pin2, Netduino1.D11_MOSI
  N4: J1.pin3, MOSFET.E
  N5: Netduino1.D13_SPCK, MOSFET.C
  N6: Netduino1.D3_TX1, MOSFET.B

notes:
  DO NOT USE MORE THEN 5V!
  Pin 1: GND
  Pin 2: SDI
  Pin 3: CLKI
  Pin 4: +5V
