# Fritzing sketch LPD8806 RGB Strip (saved by Fritzing 0.7.4b)

parts:
  VCC1 = 4 x AAA Battery Mount
  J1 = male pin header, 4 pins [form="♂ (male)"]
  Netduino1 = Netduino

nets:
  N1: VCC1.-, J1.pin1, Netduino1.GND
  N2: VCC1.+, J1.pin4
  N3: J1.pin2, Netduino1.D11_MOSI
  N4: J1.pin3, Netduino1.D13_SPCK

notes:
  DO NOT USE MORE THEN 5V!
  Pin 1: GND
  Pin 2: SDI
  Pin 3: CLKI
  Pin 4: +5V
