# Fritzing sketch Micro Serial Servo Controller (saved by Fritzing 0.7.0b)
perfboards: 1

parts:
  J1 = female pin header, 9 pins [form="♂ (male)"]
  J2 = female pin header, 9 pins [form="♂ (male)"]
  J5 = female pin header, 2 pins [form="♂ (male)"]  # not connected
  J4 = female pin header, 3 pins [form="♂ (male)"]  # not connected
  J6 = female pin header, 5 pins [form="♂ (male)"]
  Netduino1 = Netduino
  J3 = female pin header, 9 pins [form="♂ (male)"]
  J7 = Basic Servo
  J8 = Basic Servo

nets:
  N1: J1.pin1, Netduino1.GND#19
  N2: J1.pin2, J7.gnd
  N3: J1.pin3, J8.gnd
  N4: J2.pin1, Netduino1.VIN
  N5: J2.pin2, J7.vcc
  N6: J2.pin3, J8.vcc
  N7: J6.pin2, Netduino1.D0_RX0
  N8: J6.pin3, Netduino1.D1_TX0
  N9: J6.pin4, Netduino1.+5V
  N10: J6.pin5, Netduino1.GND#1
  N11: J3.pin2, J7.pulse
  N12: J3.pin3, J8.pulse
