# Fritzing sketch Multiplexing GPIOs (saved by Fritzing 0.7.0b)
breadboards: 2

parts:
  Netduino1 = Netduino
  74HC165 = IC, DIP package, 16 pins [chip_label=74HC165 spacing=300mil]
  74HC166 = IC, DIP package, 16 pins [chip_label=74HC165 spacing=300mil]
  S1 = Pushbutton [package=THT]
  R1 = Resistor [tolerance=±5% resistance=10k package="1206 [SMD]"]
  S2 = Pushbutton [package=THT]
  R2 = Resistor [tolerance=±5% resistance=10k package="1206 [SMD]"]
  S3 = Pushbutton [package=THT]
  S4 = Pushbutton [package=THT]
  S5 = Pushbutton [package=THT]
  S6 = Pushbutton [package=THT]
  S7 = Pushbutton [package=THT]
  S8 = Pushbutton [package=THT]
  R3 = Resistor [tolerance=±5% resistance=10k package="1206 [SMD]"]
  R4 = Resistor [tolerance=±5% resistance=10k package="1206 [SMD]"]
  R5 = Resistor [tolerance=±5% resistance=10k package="1206 [SMD]"]
  R6 = Resistor [tolerance=±5% resistance=10k package="1206 [SMD]"]
  R7 = Resistor [tolerance=±5% resistance=10k package="1206 [SMD]"]
  R8 = Resistor [tolerance=±5% resistance=10k package="1206 [SMD]"]
  S9 = Pushbutton [package=THT]
  S10 = Pushbutton [package=THT]
  S11 = Pushbutton [package=THT]
  S12 = Pushbutton [package=THT]
  S13 = Pushbutton [package=THT]
  S14 = Pushbutton [package=THT]
  S15 = Pushbutton [package=THT]
  S16 = Pushbutton [package=THT]
  R9 = Resistor [tolerance=±5% resistance=10k package="1206 [SMD]"]
  R10 = Resistor [tolerance=±5% resistance=10k package="1206 [SMD]"]
  R11 = Resistor [tolerance=±5% resistance=10k package="1206 [SMD]"]
  R13 = Resistor [tolerance=±5% resistance=10k package="1206 [SMD]"]
  R15 = Resistor [tolerance=±5% resistance=10k package="1206 [SMD]"]
  R16 = Resistor [tolerance=±5% resistance=10k package="1206 [SMD]"]
  R17 = Resistor [tolerance=±5% resistance=10k package="1206 [SMD]"]
  R18 = Resistor [tolerance=±5% resistance=10k package="1206 [SMD]"]
  LED1 = LED - 5mm [color="Red (633nm)" package="5 mm [THT]"]
  LED2 = LED - 5mm [color="Red (633nm)" package="5 mm [THT]"]
  LED3 = LED - 5mm [color="Red (633nm)" package="5 mm [THT]"]
  LED4 = LED - 5mm [color="Red (633nm)" package="5 mm [THT]"]
  LED5 = LED - 5mm [color="Red (633nm)" package="5 mm [THT]"]
  LED6 = LED - 5mm [color="Red (633nm)" package="5 mm [THT]"]
  LED7 = LED - 5mm [color="Red (633nm)" package="5 mm [THT]"]
  LED8 = LED - 5mm [color="Red (633nm)" package="5 mm [THT]"]
  LED9 = LED - 5mm [color="Red (633nm)" package="5 mm [THT]"]
  LED10 = LED - 5mm [color="Red (633nm)" package="5 mm [THT]"]
  LED11 = LED - 5mm [color="Red (633nm)" package="5 mm [THT]"]
  LED12 = LED - 5mm [color="Red (633nm)" package="5 mm [THT]"]
  LED13 = LED - 5mm [color="Red (633nm)" package="5 mm [THT]"]
  LED14 = LED - 5mm [color="Red (633nm)" package="5 mm [THT]"]
  LED15 = LED - 5mm [color="Red (633nm)" package="5 mm [THT]"]
  LED16 = LED - 5mm [color="Red (633nm)" package="5 mm [THT]"]
  R19 = Resistor [tolerance=±5% resistance=220 package=THT]
  R20 = Resistor [tolerance=±5% resistance=220 package=THT]
  R21 = Resistor [tolerance=±5% resistance=220 package=THT]
  R22 = Resistor [tolerance=±5% resistance=220 package=THT]
  R23 = Resistor [tolerance=±5% resistance=220 package=THT]
  R24 = Resistor [tolerance=±5% resistance=220 package=THT]
  R25 = Resistor [tolerance=±5% resistance=220 package=THT]
  R26 = Resistor [tolerance=±5% resistance=220 package=THT]
  R27 = Resistor [tolerance=±5% resistance=220 package=THT]
  R28 = Resistor [tolerance=±5% resistance=220 package=THT]
  R29 = Resistor [tolerance=±5% resistance=220 package=THT]
  R30 = Resistor [tolerance=±5% resistance=220 package=THT]
  R31 = Resistor [tolerance=±5% resistance=220 package=THT]
  R32 = Resistor [tolerance=±5% resistance=220 package=THT]
  R33 = Resistor [tolerance=±5% resistance=220 package=THT]
  R34 = Resistor [tolerance=±5% resistance=220 package=THT]
  74HC167 = IC, DIP package, 16 pins [chip_label=74HC595 spacing=300mil]
  74HC168 = IC, DIP package, 16 pins [chip_label=74HC595 spacing=300mil]
  J1 = female pin header, 31 pins [form="♀ (female)"]
  J2 = female pin header, 31 pins [form="♀ (female)"]
  J3 = female pin header, 4 pins [form="♀ (female)"]
  J4 = female pin header, 4 pins [form="♀ (female)"]
  J5 = female pin header, 4 pins [form="♀ (female)"]
  J6 = female pin header, 4 pins [form="♀ (female)"]
  J7 = female pin header, 18 pins [form="♀ (female)"]

nets:
  N1: Netduino1.D13_SPCK, 74HC165.pin2
  N2: Netduino1.D12_MISO, 74HC165.pin9
  N3: Netduino1.D11_MOSI, 74HC167.pin14
  N4: Netduino1.D10_PWM3, 74HC165.pin1
  N5: Netduino1.D9_PWM2, 74HC167.pin12
  N6: Netduino1.3V3, 74HC165.pin16, 74HC166.pin16
  N7: Netduino1.GND, 74HC165.pin8, 74HC165.pin15, 74HC166.pin8, 74HC166.pin15
  N8: 74HC165.pin3, J6.pin1
  N9: 74HC165.pin4, J6.pin2
  N10: 74HC165.pin5, J6.pin3
  N11: 74HC165.pin6, J6.pin4
  N12: 74HC165.pin10, 74HC166.pin9
  N13: 74HC165.pin11, J4.pin4
  N14: 74HC165.pin12, J4.pin3
  N15: 74HC165.pin13, J4.pin2
  N16: 74HC165.pin14, J4.pin1
  N17: 74HC166.pin3, J5.pin1
  N18: 74HC166.pin4, J5.pin2
  N19: 74HC166.pin5, J5.pin3
  N20: 74HC166.pin6, J5.pin4
  N21: 74HC166.pin11, J3.pin4
  N22: 74HC166.pin12, J3.pin3
  N23: 74HC166.pin13, J3.pin2
  N24: 74HC166.pin14, J3.pin1
  N25: S1.leg0, S2.leg0, S3.leg0, S4.leg0, S5.leg0, S6.leg0, S7.leg0, S8.leg0, S9.leg0, S10.leg0, S11.leg0, S12.leg0, S13.leg0, S14.leg0, S15.leg0, S16.leg0, R19.Pin_1, R20.Pin_1, R21.Pin_1, R22.Pin_1, R23.Pin_1, R24.Pin_1, R25.Pin_1, R26.Pin_1, R27.Pin_1, R28.Pin_1, R29.Pin_1, R30.Pin_1, R31.Pin_1, R32.Pin_1, R33.Pin_1, R34.Pin_1
  N26: S1.leg1, R1.Pin_1, J2.pin29
  N27: R1.Pin_0, R2.Pin_0, R3.Pin_0, R4.Pin_0, R5.Pin_0, R6.Pin_0, R7.Pin_0, R8.Pin_0, R9.Pin_0, R10.Pin_0, R11.Pin_0, R13.Pin_0, R15.Pin_0, R16.Pin_0, R17.Pin_0, R18.Pin_0
  N28: S2.leg1, R2.Pin_1, J2.pin27
  N29: S3.leg1, R3.Pin_1, J2.pin25
  N30: S4.leg1, R4.Pin_1, J2.pin23
  N31: S5.leg1, R5.Pin_1, J2.pin21
  N32: S6.leg1, R6.Pin_1, J2.pin19
  N33: S7.leg1, R7.Pin_1, J2.pin17
  N34: S8.leg1, R8.Pin_1, J2.pin15
  N35: S9.leg1, R9.Pin_1, J2.pin13
  N36: S10.leg1, R16.Pin_1, J2.pin9
  N37: S11.leg1, R15.Pin_1, J2.pin7
  N38: S12.leg1, R18.Pin_1, J2.pin31
  N39: S13.leg1, R17.Pin_1, J2.pin1
  N40: S14.leg1, R11.Pin_1, J2.pin5
  N41: S15.leg1, R13.Pin_1, J2.pin11
  N42: S16.leg1, R10.Pin_1, J2.pin3
  N43: LED1.cathode, R34.Pin_0
  N44: LED1.anode, J1.pin1
  N45: LED2.cathode, R19.Pin_0
  N46: LED2.anode, J1.pin3
  N47: LED3.cathode, R20.Pin_0
  N48: LED3.anode, J1.pin5
  N49: LED4.cathode, R21.Pin_0
  N50: LED4.anode, J1.pin7
  N51: LED5.cathode, R22.Pin_0
  N52: LED5.anode, J1.pin9
  N53: LED6.cathode, R26.Pin_0
  N54: LED6.anode, J1.pin15
  N55: LED7.cathode, R24.Pin_0
  N56: LED7.anode, J1.pin13
  N57: LED8.cathode, R23.Pin_0
  N58: LED8.anode, J1.pin11
  N59: LED9.cathode, R25.Pin_0
  N60: LED9.anode, J1.pin17
  N61: LED10.cathode, R27.Pin_0
  N62: LED10.anode, J1.pin23
  N63: LED11.cathode, R28.Pin_0
  N64: LED11.anode, J1.pin21
  N65: LED12.cathode, R32.Pin_0
  N66: LED12.anode, J1.pin27
  N67: LED13.cathode, R33.Pin_0
  N68: LED13.anode, J1.pin29
  N69: LED14.cathode, R29.Pin_0
  N70: LED14.anode, J1.pin25
  N71: LED15.cathode, R30.Pin_0
  N72: LED15.anode, J1.pin19
  N73: LED16.cathode, R31.Pin_0
  N74: LED16.anode, J1.pin31
  N75: 74HC167.pin1, J7.pin12
  N76: 74HC167.pin2, J7.pin13
  N77: 74HC167.pin3, J7.pin14
  N78: 74HC167.pin4, J7.pin15
  N79: 74HC167.pin5, J7.pin16
  N80: 74HC167.pin6, J7.pin17
  N81: 74HC167.pin7, J7.pin18
  N82: 74HC167.pin8, 74HC167.pin13, 74HC168.pin8, 74HC168.pin13
  N83: 74HC167.pin9, 74HC168.pin14
  N84: 74HC167.pin10, 74HC167.pin16, 74HC168.pin10, 74HC168.pin16
  N85: 74HC167.pin15, J7.pin11
  N86: 74HC168.pin1, J7.pin2
  N87: 74HC168.pin2, J7.pin3
  N88: 74HC168.pin3, J7.pin4
  N89: 74HC168.pin4, J7.pin5
  N90: 74HC168.pin5, J7.pin6
  N91: 74HC168.pin6, J7.pin7
  N92: 74HC168.pin7, J7.pin8
  N93: 74HC168.pin15, J7.pin1

notes:
  Inputs
  Outputs
