# Fritzing sketch NES Controller Adapter (saved by Fritzing 0.7.10b)
perfboards: 1

parts:
  Netduino1 = Netduino
  J1 = male pin header, 6 pins [form="♂ (male)"]

nets:
  N1: Netduino1.+5V, J1.pin2
  N2: Netduino1.GND, J1.pin1
  N3: Netduino1.A2, J1.pin6
  N4: Netduino1.A3, J1.pin5
  N5: Netduino1.A4_TWD, J1.pin4
  N6: Netduino1.A5_TWCK, J1.pin3
