# Fritzing sketch Rdm630 RFID Reader (saved by Fritzing 0.7.0b)
perfboards: 1

parts:
  J1 = female pin header, 5 pins [form="♂ (male)"]
  J2 = female pin header, 2 pins [form="♂ (male)"]
  J3 = female pin header, 3 pins [form="♂ (male)"]  # not connected
  Netduino1 = Netduino
  ANT1 = Antenna

nets:
  N1: J1.pin1, Netduino1.+5V
  N2: J1.pin2, Netduino1.GND
  N3: J1.pin4, Netduino1.D1_TX0
  N4: J1.pin5, Netduino1.D0_RX0
  N5: J2.pin1, J2.pin2, ANT1.antenna_lead
