# Fritzing sketch Rotary Encoder (saved by Fritzing 0.7.0b)
breadboards: 1

parts:
  R1 = Rotary Potentiometer (Large) [maximum_resistance=100kΩ package=THT]
  Netduino1 = Netduino

nets:
  N1: R1.leg1, Netduino1.D0_RX0
  N2: R1.wiper, Netduino1.GND
  N3: R1.leg2, Netduino1.D1_TX0
