# Fritzing sketch Sound Module (saved by Fritzing 0.7.0b)
breadboards: 1

parts:
  Netduino1 = Netduino
  IC1 = IC, DIP package, 14 pins [chip_label=SOMO-14D spacing=600mil]
  SPKR1 = Loudspeaker

nets:
  N1: Netduino1.D2_RX1, IC1.pin12
  N2: Netduino1.D1_TX0, IC1.pin11
  N3: Netduino1.D0_RX0, IC1.pin10
  N4: Netduino1.3V3, IC1.pin1
  N5: Netduino1.GND, IC1.pin2
  N6: IC1.pin4, SPKR1.pin2
  N7: IC1.pin5, SPKR1.pin1
