# Fritzing sketch TMP36 Temperature sensor (saved by Fritzing 0.7.0b)
breadboards: 1

parts:
  T1 = TMP36 Temperature Sensor [package="TO92 [THT]"]
  Netduino1 = Netduino

nets:
  N1: T1.+Vs, Netduino1.3V3
  N2: T1.Vout, Netduino1.A4_TWD
  GND: T1.GND, Netduino1.GND
