# Fritzing sketch Thermal Printer (saved by Fritzing 0.7.10b)

parts:
  Onderdeel1 = Thermal Printer
  Netduino1 = Netduino
  5V_Power_Supply = 4 x AAA Battery Mount

nets:
  GND: Onderdeel1.GND, Netduino1.GND, 5V_Power_Supply.-
  N1: Onderdeel1.VH, 5V_Power_Supply.+
  N2: Onderdeel1.RXD, Netduino1.D1_TX0
  N3: Onderdeel1.TXD, Netduino1.D0_RX0
