# Fritzing sketch Wii Nunchuk (saved by Fritzing 0.7.4b)
breadboards: 1
perfboards: 1

parts:
  Netduino1 = Netduino
  J1 = male pin header, 4 pins [form="♂ (male)"]
  R1 = Resistor [tolerance=±5% resistance=10k package=THT]
  R2 = Resistor [tolerance=±5% resistance=10k package=THT]

nets:
  N1: Netduino1.GND, J1.pin1
  N2: Netduino1.3V3, J1.pin2, R1.Pin_1, R2.Pin_1
  N3: Netduino1.A4_TWD, J1.pin3, R2.Pin_0
  N4: Netduino1.A5_TWCK, J1.pin4, R1.Pin_0
